# Fritzing sketch stopwatch-arduino (saved by Fritzing 0.7.12b)
breadboards: 1

parts:
  LCD1 = LCD screen
  R1 = Resistor [tolerance=±5% resistance=220 package=THT]
  S2 = Pushbutton [package="[THT]"]
  R2 = Resistor [tolerance=±5% resistance=100 package=THT]
  R3 = Resistor [tolerance=±5% resistance=100 package=THT]
  Arduino1 = Arduino
  S1 = Pushbutton [package="[THT]"]

nets:
  VSS: LCD1.VSS, LCD1.R/W, LCD1.LED-, R1.Pin_0, R2.Pin_1, R3.Pin_1, Arduino1.GND
  VDD: LCD1.VDD, S2.Pin_3, S2.Pin_4, Arduino1.+5V, S1.Pin_3, S1.Pin_4
  N1: LCD1.V0, R1.Pin_1
  N2: LCD1.RS, Arduino1.D7
  N3: LCD1.E, Arduino1.D8
  N4: LCD1.DB4, Arduino1.D9
  N5: LCD1.DB5, Arduino1.D10
  N6: LCD1.DB6, Arduino1.D11
  N7: LCD1.DB7, Arduino1.D12
  N8: LCD1.LED+, Arduino1.D6
  N9: S2.Pin_1, S2.Pin_2, R3.Pin_0, Arduino1.D1TX
  N10: R2.Pin_0, Arduino1.D0RX, S1.Pin_1, S1.Pin_2
