# Fritzing sketch stopwatch-board (saved by Fritzing 0.8.0b)
breadboards: 1

parts:
  LCD1 = LCD screen
  XTAL1 = Crystal [frequency="16 Mhz" package=THT]
  IC1 = IC, DIP package, 14 pins [chip_label=ATTiny84]
  S2 = Pushbutton [package="[THT]"]
  C3 = Ceramic Capacitor [capacitance=100nF package="100 mil [THT, multilayer]"]
  C4 = Ceramic Capacitor [capacitance=100nF package="100 mil [THT, multilayer]"]
  R5 = Resistor [tolerance=±5% resistance=220 package=THT]
  R6 = Resistor [tolerance=±5% resistance=220 package=THT]
  R4 = Trimmer Potentiometer [maximum_resistance=10kΩ package=THT]
  S3 = Pushbutton [package="[THT]"]
  J1 = rounded female pin header, 2 pins [form="♀ (female rounded)"]
  C5 = Ceramic Capacitor [capacitance=100nF package="100 mil [THT, multilayer]"]

nets:
  GND: LCD1.VSS, LCD1.R/W, LCD1.LED-, IC1.pin14, C3.0, C4.1, R5.Pin_0, R6.Pin_0, R4.wiper, J1.pin2, C5.1
  N1: LCD1.VDD, IC1.pin1, IC1.pin4, S2.Pin_1, S2.Pin_2, S3.Pin_1, S3.Pin_2, J1.pin1, C5.0
  N2: LCD1.V0, R4.leg1
  N3: LCD1.RS, IC1.pin13
  N4: LCD1.E, IC1.pin12
  N5: LCD1.DB4, IC1.pin11
  N6: LCD1.DB5, IC1.pin10
  N7: LCD1.DB6, IC1.pin9
  N8: LCD1.DB7, IC1.pin8
  N9: LCD1.LED+, IC1.pin7
  N10: XTAL1.pin_0, IC1.pin2, C3.1
  N11: XTAL1.pin_1, IC1.pin3, C4.0
  N12: IC1.pin5, S2.Pin_3, S2.Pin_4, R6.Pin_1
  N13: IC1.pin6, R5.Pin_1, S3.Pin_3, S3.Pin_4

notes:
  woozle.org/derby
